// Digital circuit 02_f.dig as structural Verilog
module _02_f (
  input  A,
  input  B,
  output Output
);

  wire and_1_out, and_2_out, not_1_out, not_2_out;

  not not_1 (not_1_out, A);
  and and_1 (and_1_out, not_1_out, B);
  and and_2 (and_2_out, A, not_2_out);
  not not_2 (not_2_out, B);
  or or_1 (Output, and_1_out, and_2_out);
endmodule
