// Digital circuit Template.dig as structural Verilog
module Template (
  input  B,
  input  A,
  input  D,
  input  C,
  output Z1,
  output Z2,
  output Z3
);

  wire and_1_out, and_2_out, and_3_out, and_4_out, and_5_out, and_6_out, not_1_out, not_2_out, not_3_out,
       not_4_out, xnor_1_out, xnor_2_out;

  not not_1 (not_1_out, B);
  not not_2 (not_2_out, A);
  not not_3 (not_3_out, D);
  not not_4 (not_4_out, C);
  xnor xnor_1 (xnor_1_out, A, C);
  xnor xnor_2 (xnor_2_out, B, D);
  and and_1 (and_1_out, not_2_out, C);
  and and_2 (and_2_out, not_2_out, not_1_out, D);
  and and_3 (and_3_out, not_1_out, C, D);
  and and_4 (and_4_out, B, not_4_out, not_3_out);
  and and_5 (and_5_out, A, B, not_3_out);
  and and_6 (and_6_out, A, not_4_out);
  and and_7 (Z3, xnor_1_out, xnor_2_out);
  or or_1 (Z2, and_1_out, and_2_out, and_3_out);
  or or_2 (Z1, and_4_out, and_5_out, and_6_out);
endmodule
