// Digital circuit f.dig as structural Verilog
module f (
  input  B,
  input  A,
  input  D,
  input  C,
  output Z1,
  output Z2,
  output Z3
);

  wire and_1_out, and_2_out, and_3_out, and_4_out, and_5_out, and_6_out, and_7_out, and_8_out, and_9_out,
       and_10_out, not_1_out, not_2_out, not_3_out, not_4_out, or_1_out, or_2_out, or_3_out, or_4_out;

  not not_1 (not_1_out, B);
  not not_2 (not_2_out, A);
  not not_3 (not_3_out, D);
  not not_4 (not_4_out, C);
  or or_1 (or_1_out, not_2_out, not_1_out);
  or or_2 (or_2_out, D, C);
  or or_3 (or_3_out, B, A);
  or or_4 (or_4_out, not_4_out, not_3_out);
  and and_1 (and_1_out, B, A, D, C);
  and and_2 (and_2_out, B, not_2_out, D, not_4_out);
  and and_3 (and_3_out, not_1_out, A, not_3_out, C);
  and and_4 (and_4_out, not_1_out, not_2_out, not_3_out, not_4_out);
  and and_5 (and_5_out, not_3_out, or_3_out, not_4_out);
  and and_6 (and_6_out, B, or_4_out, A);
  and and_7 (and_7_out, B, not_2_out, not_3_out, not_4_out);
  and and_8 (and_8_out, C, or_1_out, D);
  and and_9 (and_9_out, not_1_out, or_2_out, not_2_out);
  and and_10 (and_10_out, D, not_4_out, not_1_out, A);
  or or_5 (Z3, and_1_out, and_2_out, and_3_out, and_4_out);
  or or_6 (Z1, and_5_out, and_6_out, and_7_out);
  or or_7 (Z2, and_8_out, and_9_out, and_10_out);
endmodule
