// Digital circuit Template.dig as structural Verilog
module Template (
  input  A,
  input  B,
  input  C,
  input  D,
  output Z1,
  output Z2,
  output Z3
);

  wire a_t, b_t, c_t, d_t, or_1_out, or_2_out, or_3_out, or_4_out, or_5_out, or_6_out, or_7_out, or_8_out,
       or_9_out, or_10_out, xnor_1_out, xnor_2_out;

  not not_1 (c_t, C);
  not not_2 (d_t, D);
  not not_3 (a_t, A);
  not not_4 (b_t, B);
  or or_1 (or_1_out, C, D);
  or or_2 (or_2_out, b_t, D);
  or or_3 (or_3_out, a_t, b_t);
  or or_4 (or_4_out, D, c_t, B, a_t);
  or or_5 (or_5_out, d_t, C, b_t, A);
  or or_6 (or_6_out, c_t, d_t);
  or or_7 (or_7_out, d_t, B);
  or or_8 (or_8_out, A, B);
  or or_9 (or_9_out, D, c_t, B, a_t);
  or or_10 (or_10_out, d_t, C, b_t, A);
  xnor xnor_1 (xnor_1_out, A, C);
  xnor xnor_2 (xnor_2_out, B, D);
  and and_1 (Z3, xnor_1_out, xnor_2_out);
  and and_2 (Z2, or_1_out, or_2_out, or_3_out, or_4_out, or_5_out);
  and and_3 (Z1, or_6_out, or_7_out, or_8_out, or_9_out, or_10_out);
endmodule
