// Digital circuit Template.dig as structural Verilog
module Template (
  input  X0,
  input  X1,
  input  Selector,
  output Z
);

  wire and_1_out, and_2_out, and_3_out, s_t, x0_t, x1_t;

  not not_1 (x0_t, X0);
  not not_2 (x1_t, X1);
  not not_3 (s_t, Selector);
  and and_1 (and_1_out, x0_t, X1, Selector);
  and and_2 (and_2_out, X0, x1_t, s_t);
  and and_3 (and_3_out, X0, X1);
  or or_1 (Z, and_1_out, and_2_out, and_3_out);

  // Other names for the same wires on the sheet: s = Selector
endmodule
