// Digital circuit Template.dig as structural Verilog
module Template (
  input  X0,
  input  X1,
  input  Selector,
  output Z
);

  wire or_1_out, or_2_out, or_3_out, s_t, x0_t, x1_t;

  not not_1 (x0_t, X0);
  not not_2 (x1_t, X1);
  not not_3 (s_t, Selector);
  or or_1 (or_1_out, x0_t, X1, s_t);
  or or_2 (or_2_out, X0, x1_t, Selector);
  or or_3 (or_3_out, X0, X1);
  and and_1 (Z, or_1_out, or_2_out, or_3_out);

  // Other names for the same wires on the sheet: s = Selector
endmodule
