// Digital circuit Template-01.dig as structural Verilog
module Template_01 (
  input  [3:0] In,
  input  in_9,
  output A,
  output B,
  output C,
  output D,
  output E,
  output F,
  output G
);

  wire _0, _1, _2, _3, _4, _5, _6, _7, _8, _9;

  Demultiplexer #(.Selector_Bits(4)) demultiplexer_1 (
    .sel(In), .in(in_9), .out_0(_0), .out_1(_1), .out_2(_2), .out_3(_3), .out_4(_4), .out_5(_5), .out_6(_6),
    .out_7(_7), .out_8(_8), .out_9(_9));  // open: out_10, out_11, out_12, out_13, out_14, out_15
  or or_1 (A, _0, _2, _3, _9, _5, _6, _7, _8);
  or or_2 (B, _0, _2, _3, _4, _1, _7, _8, _9);
  or or_3 (C, _0, _1, _3, _4, _5, _6, _7, _8, _9);
  or or_4 (D, _0, _2, _3, _5, _6, _8, _9);
  or or_5 (E, _0, _2, _6, _8);
  or or_6 (F, _0, _4, _5, _6, _7, _8, _9);
  or or_7 (G, _2, _4, _5, _6, _3, _8, _9);

  // Notes on the sheet:
  //   in_9: default 1
endmodule
