// Digital circuit Template-03.dig as structural Verilog
module Template_03 (
  input  [3:0] In,
  input  [1:0] Selector,
  output [3:0] Output
);

  wire [3:0] multiplexer_1_out, multiplexer_2_out, multiplexer_3_out, multiplexer_4_out;

  Multiplexer #(.Selector_Bits(4), .Bits(4)) multiplexer_1 (
    .sel(In), .in_0(4'b0000), .in_1(4'b0001), .in_2(4'b0011), .in_3(4'b0010), .in_4(4'b0110), .in_5(4'b0111),
    .in_6(4'b0101), .in_7(4'b0100), .in_8(4'b1100), .in_9(4'b1101), .in_10(4'b0001), .in_11(4'b0001),
    .in_12(4'b0001), .in_13(4'b0001), .in_14(4'b0001), .in_15(4'b0001), .out(multiplexer_1_out));
  Multiplexer #(.Selector_Bits(4), .Bits(4)) multiplexer_2 (
    .sel(In), .in_0(4'b0000), .in_1(4'b0101), .in_2(4'b0010), .in_3(4'b1001), .in_4(4'b0100), .in_5(4'b1011),
    .in_6(4'b0110), .in_7(4'b1101), .in_8(4'b1010), .in_9(4'b1111), .in_10(4'b0001), .in_11(4'b0001),
    .in_12(4'b0001), .in_13(4'b0001), .in_14(4'b0001), .in_15(4'b0001), .out(multiplexer_2_out));
  Multiplexer #(.Bits(4), .Selector_Bits(4)) multiplexer_3 (
    .sel(In), .in_0(4'b0011), .in_1(4'b0100), .in_2(4'b0101), .in_3(4'b0110), .in_4(4'b0111), .in_5(4'b1000),
    .in_6(4'b1001), .in_7(4'b1010), .in_8(4'b1011), .in_9(4'b1100), .in_10(4'b0001), .in_11(4'b0001),
    .in_12(4'b0001), .in_13(4'b0001), .in_14(4'b0001), .in_15(4'b0001), .out(multiplexer_3_out));
  Multiplexer #(.Selector_Bits(4), .Bits(4)) multiplexer_4 (
    .sel(In), .in_0(4'b0000), .in_1(4'b0001), .in_2(4'b0010), .in_3(4'b0011), .in_4(4'b0100), .in_5(4'b1011),
    .in_6(4'b1100), .in_7(4'b1101), .in_8(4'b1110), .in_9(4'b1111), .in_10(4'b0001), .in_11(4'b0001),
    .in_12(4'b0001), .in_13(4'b0001), .in_14(4'b0001), .in_15(4'b0001), .out(multiplexer_4_out));
  Multiplexer #(.Bits(4), .Selector_Bits(2)) multiplexer_5 (
    .sel(Selector), .in_0(multiplexer_3_out), .in_1(multiplexer_1_out), .in_2(multiplexer_4_out),
    .in_3(multiplexer_2_out), .out(Output));
endmodule
