// Digital circuit Template-04.dig as structural Verilog
module Template_04 (
  input  [6:0] In,
  output [6:0] Output
);

  wire [0:0] not_7_out;
  wire [1:1] not_6_out;
  wire [2:0] c;
  wire [2:2] not_5_out;
  wire [3:3] not_4_out;
  wire [4:4] not_3_out;
  wire [5:5] not_2_out;
  wire [6:6] not_1_out;

  xor xor_1 (c[2], In[3], In[2], In[1], In[0]);
  xor xor_2 (c[1], In[5], In[4], In[1], In[0]);
  xor xor_3 (c[0], In[6], In[4], In[2], In[0]);
  not not_1 (not_1_out[6], In[6]);
  not not_2 (not_2_out[5], In[5]);
  not not_3 (not_3_out[4], In[4]);
  not not_4 (not_4_out[3], In[3]);
  not not_5 (not_5_out[2], In[2]);
  not not_6 (not_6_out[1], In[1]);
  not not_7 (not_7_out[0], In[0]);
  Multiplexer #(.Bits(7), .Selector_Bits(3)) multiplexer_1 (
    .sel(c), .in_0(In), .in_1({not_1_out[6], In[5:0]}), .in_2({In[6], not_2_out[5], In[4:0]}),
    .in_3({In[6:5], not_3_out[4], In[3:0]}), .in_4({In[6:4], not_4_out[3], In[2:0]}),
    .in_5({In[6:3], not_5_out[2], In[1:0]}), .in_6({In[6:2], not_6_out[1], In[0]}),
    .in_7({In[6:1], not_7_out[0]}), .out(Output));

  // Other names for the same wires on the sheet: c1 = c[2]; c2 = c[1]; c3 = c[0]; _7 = In[0]; _6 = In[1]; _5 = In[2];
  //   _4 = In[3]; _3 = In[4]; _2 = In[5]; _1 = In[6]
endmodule
