// Digital circuit fuji04.dig as structural Verilog
module fuji04 (
  input  [6:0] In,
  output [6:0] Output
);

  wire a, b, c, d, e, f, g, not_1_out, not_2_out, not_3_out, not_4_out, not_5_out, not_6_out, not_7_out;
  wire [2:0] xor_3_out;

  xor xor_1 (xor_3_out[2], In[0], In[1], In[2], In[3]);
  xor xor_2 (xor_3_out[1], In[5], In[4], In[0], In[1]);
  xor xor_3 (xor_3_out[0], In[6], In[4], In[2], In[0]);
  Multiplexer #(.Bits(7), .Selector_Bits(3)) multiplexer_1 (
    .sel(xor_3_out), .in_0({7{1'b0}}), .in_1(7'b1000000), .in_2(7'b0100000), .in_3(7'b0010000),
    .in_4(7'b0001000), .in_5(7'b0000100), .in_6(7'b0000010), .in_7(7'b0000001), .out({g, f, e, d, c, b, a}));
  Multiplexer multiplexer_2 (.sel(a), .in_0(In[0]), .in_1(not_1_out), .out(Output[0]));
  not not_1 (not_1_out, In[0]);
  Multiplexer multiplexer_3 (.sel(b), .in_0(In[1]), .in_1(not_2_out), .out(Output[1]));
  not not_2 (not_2_out, In[1]);
  Multiplexer multiplexer_4 (.sel(c), .in_0(In[2]), .in_1(not_3_out), .out(Output[2]));
  not not_3 (not_3_out, In[2]);
  Multiplexer multiplexer_5 (.sel(d), .in_0(In[3]), .in_1(not_4_out), .out(Output[3]));
  not not_4 (not_4_out, In[3]);
  Multiplexer multiplexer_6 (.sel(e), .in_0(In[4]), .in_1(not_5_out), .out(Output[4]));
  not not_5 (not_5_out, In[4]);
  Multiplexer multiplexer_7 (.sel(f), .in_0(In[5]), .in_1(not_6_out), .out(Output[5]));
  not not_6 (not_6_out, In[5]);
  Multiplexer multiplexer_8 (.sel(g), .in_0(In[6]), .in_1(not_7_out), .out(Output[6]));
  not not_7 (not_7_out, In[6]);
endmodule
