// Digital circuit 05 (1).dig as structural Verilog
module _05__1 (
  input  T,
  input  Clear,
  input  Clock,
  output Q,
  output Q_2
);

  wire driverinvsel_1_out, nor_1_out, nor_2_out, nor_3_out, nor_4_out, not_1_out, xor_1_out;

  xor xor_1 (xor_1_out, T, Q);
  not not_1 (not_1_out, Clock);
  nor nor_1 (nor_1_out, nor_4_out, nor_2_out);
  nor nor_2 (nor_2_out, nor_1_out, not_1_out);
  nor nor_3 (nor_3_out, nor_2_out, not_1_out, nor_4_out);
  nor nor_4 (nor_4_out, nor_3_out, driverinvsel_1_out);
  assign driverinvsel_1_out = ~Clear ? xor_1_out : 1'bz;  // DriverInvSel driverinvsel_1
  PullDown pulldown_1 (.out(driverinvsel_1_out));
  nor nor_5 (Q, nor_2_out, Q_2);
  nor nor_6 (Q_2, Q, nor_3_out);
endmodule
