// Digital circuit gcd_template.dig as structural Verilog
module gcd_template (
  input  [7:0] A,
  input  [7:0] B,
  input  start,
  input  clear,
  input  clk,
  output busy,
  output [7:0] \output ,
  output out_8
);

  wire comparator_1_eq, comparator_1_gt, comparator_1_lt, not_1_out;
  wire [7:0] a_t, aa, b_t, bb, multiplexer_1_out, multiplexer_2_out, sub_1_s, sub_2_s;

  Multiplexer #(.Bits(8)) multiplexer_1 (.sel(out_8), .in_0(A), .in_1(aa), .out(multiplexer_1_out));
  Multiplexer #(.Bits(8)) multiplexer_2 (.sel(out_8), .in_0(B), .in_1(bb), .out(multiplexer_2_out));
  T_FF t_ff_1 (.T(start), .C(clk), .Q(out_8));  // open: nQ
  D_FF #(.Bits(8)) d_ff_1 (.D(multiplexer_1_out), .C(clk), .Q(a_t));  // open: nQ
  D_FF #(.Bits(8)) d_ff_2 (.D(multiplexer_2_out), .C(clk), .Q(b_t));  // open: nQ
  Sub #(.Bits(8)) sub_1 (.a(a_t), .b(b_t), .c_i(1'b0), .s(sub_1_s));  // open: c_o
  Comparator #(.Bits(8)) comparator_1 (
    .a(a_t), .b(b_t), .gt(comparator_1_gt), .eq(comparator_1_eq), .lt(comparator_1_lt));
  Sub #(.Bits(8)) sub_2 (.a(b_t), .b(a_t), .c_i(1'b0), .s(sub_2_s));  // open: c_o
  Multiplexer #(.Bits(8)) multiplexer_3 (.sel(comparator_1_gt), .in_0(a_t), .in_1(sub_1_s), .out(aa));
  Multiplexer #(.Bits(8)) multiplexer_4 (.sel(comparator_1_lt), .in_0(b_t), .in_1(sub_2_s), .out(bb));
  Multiplexer #(.Bits(8)) multiplexer_5 (.sel(comparator_1_eq), .in_0({8{1'b0}}), .in_1(a_t), .out(\output ));
  not not_1 (not_1_out, comparator_1_eq);
  D_FF d_ff_3 (.D(not_1_out), .C(clk), .Q(busy));  // open: nQ

  // Other names for the same wires on the sheet: start_t = out_8
endmodule

/* Test case t1:
A B start clear clk busy output
0xF 0x6 0 0 0 0 0
0xF 0x6 0 0 1 X 0
0xF 0x6 1 0 0 X 0
0xF 0x6 1 0 1 X 0
0xF 0x6 1 0 0 X 0
loop(x,1000)
0xF 0x6 0 0 1 X X
0xF 0x6 0 0 0 X X
end loop
0xF 0x6 0 0 0 0 0x3
*/
