// Digital circuit template.dig as structural Verilog
module template (
  input  reset,
  input  clk,
  output A,
  output B,
  output C
);

  wire and_1_out, and_2_out, and_3_out, and_4_out, and_5_out, not_1_out, not_2_out, not_3_out, not_4_out,
       or_1_out;

  D_FF d_ff_1 (.D(and_1_out), .C(clk), .Q(C));  // open: nQ
  and and_1 (and_1_out, not_1_out, A);
  not not_1 (not_1_out, reset);
  and and_2 (and_2_out, not_2_out, or_1_out);
  not not_2 (not_2_out, reset);
  D_FF d_ff_2 (.D(and_2_out), .C(clk), .Q(B));  // open: nQ
  or or_1 (or_1_out, not_3_out, and_3_out);
  not not_3 (not_3_out, B);
  and and_3 (and_3_out, ~A, ~C);  // And
  D_FF d_ff_3 (.D(and_4_out), .C(clk), .Q(A));  // open: nQ
  and and_4 (and_4_out, not_4_out, and_5_out);
  not not_4 (not_4_out, reset);
  and and_5 (and_5_out, B, ~C);  // And
endmodule

/* Test case t1:
clk reset C B A
0 0 0 0 0 
0 1 0 0 0
1 1 0 0 0
0 0 0 0 0
1 0 0 1 0
0 0 0 1 0
1 0 0 1 1
0 0 0 1 1
1 0 1 0 1
0 0 1 0 1
1 0 1 1 0
0 0 1 1 0
1 0 0 0 0
0 0 0 0 0
1 0 0 1 0
0 0 0 1 0
1 0 0 1 1
0 0 0 1 1
1 0 1 0 1
0 0 1 0 1
1 0 1 1 0
0 0 1 1 0
1 0 0 0 0
0 0 0 0 0
*/
