// Digital circuit templatekitty.dig as structural Verilog
module templatekitty (
  input  reset,
  input  clk,
  output A,
  output B,
  output C
);

  wire and_1_out, and_2_out, and_3_out, and_4_out, and_5_out, not_1_out, not_2_out, not_3_out, not_4_out,
       not_5_out, not_6_out, not_7_out, not_8_out, not_9_out, not_10_out, not_11_out, or_1_out, or_2_out;

  and and_1 (and_1_out, not_1_out, A, not_2_out, C);
  not not_1 (not_1_out, reset);
  not not_2 (not_2_out, B);
  and and_2 (and_2_out, not_3_out, A, B, not_4_out);
  not not_3 (not_3_out, reset);
  not not_4 (not_4_out, C);
  and and_3 (and_3_out, not_5_out, not_6_out, not_7_out);
  not not_5 (not_5_out, reset);
  not not_6 (not_6_out, A);
  not not_7 (not_7_out, C);
  and and_4 (and_4_out, not_8_out, A, not_9_out, C);
  not not_8 (not_8_out, reset);
  not not_9 (not_9_out, B);
  and and_5 (and_5_out, not_10_out, B, not_11_out);
  not not_10 (not_10_out, reset);
  not not_11 (not_11_out, C);
  or or_1 (or_1_out, and_1_out, and_2_out);
  or or_2 (or_2_out, and_3_out, and_4_out);
  D_FF d_ff_1 (.D(or_1_out), .C(clk), .Q(C));  // open: nQ
  D_FF d_ff_2 (.D(or_2_out), .C(clk), .Q(B));  // open: nQ
  D_FF d_ff_3 (.D(and_5_out), .C(clk), .Q(A));  // open: nQ
endmodule

/* Test case:
clk reset C B A
0 0 0 0 0 
0 1 0 0 0
1 1 0 0 0
0 0 0 0 0
1 0 0 1 0
0 0 0 1 0
1 0 0 1 1
0 0 0 1 1
1 0 1 0 1
0 0 1 0 1
1 0 1 1 0
0 0 1 1 0
1 0 0 0 0
0 0 0 0 0
1 0 0 1 0
0 0 0 1 0
1 0 0 1 1
0 0 0 1 1
1 0 1 0 1
0 0 1 0 1
1 0 1 1 0
0 0 1 1 0
1 0 0 0 0
0 0 0 0 0
*/
