// Digital circuit Exam1_01_Template.dig as structural Verilog
module Exam1_01_Template (
  input  X1,
  input  X2,
  input  X3,
  input  X4,
  output Y1,
  output [4:0] CheckGlitch
);

  wire and_1_out, and_2_out, and_3_out, and_4_out;

  and and_1 (and_1_out, X3, X4, X2);
  and and_2 (and_2_out, X1, X2, ~X3);  // And
  and and_3 (and_3_out, X1, ~X2, ~X3);  // And
  and and_4 (and_4_out, X1, X4, X2);
  or or_1 (Y1, and_1_out, and_2_out, and_3_out, and_4_out);
  Counter #(.Bits(5)) counter_1 (.en(1'b1), .C(Y1), .clr(1'b0), .out(CheckGlitch));  // open: ovf

  // Notes on the sheet:
  //   Must not change this section
endmodule

/* Test case t1:
X1 X2 X3 X4 Y1
0 0 0 0 0
0 0 0 1 0
0 0 1 0 0
0 0 1 1 0
0 1 0 0 0
0 1 0 1 0
0 1 1 0 0
0 1 1 1 1
1 0 0 0 1
1 0 0 1 1
1 0 1 0 0
1 0 1 1 0
1 1 0 0 1
1 1 0 1 1
1 1 1 0 0
1 1 1 1 1
*/
