// Digital circuit Exam1_2_Template.dig as structural Verilog
module Exam1_2_Template (
  input  X1,
  input  X0,
  input  Y1,
  input  Y0,
  output [4:0] Z
);

  wire [4:0] multiplexer_1_out, multiplexer_2_out, multiplexer_3_out, multiplexer_4_out;

  Multiplexer #(.Selector_Bits(2), .Bits(5)) multiplexer_1 (
    .sel({Y1, Y0}), .in_0(5'b00001), .in_1({5{1'b0}}), .in_2({5{1'b0}}), .in_3({5{1'b0}}),
    .out(multiplexer_1_out));
  Multiplexer #(.Selector_Bits(2), .Bits(5)) multiplexer_2 (
    .sel({Y1, Y0}), .in_0(5'b00001), .in_1(5'b00001), .in_2(5'b00001), .in_3(5'b00001),
    .out(multiplexer_2_out));
  Multiplexer #(.Selector_Bits(2), .Bits(5)) multiplexer_3 (
    .sel({Y1, Y0}), .in_0(5'b00001), .in_1(5'b00010), .in_2(5'b00100), .in_3(5'b01000),
    .out(multiplexer_3_out));
  Multiplexer #(.Selector_Bits(2), .Bits(5)) multiplexer_4 (
    .sel({Y1, Y0}), .in_0(5'b00001), .in_1(5'b00011), .in_2(5'b01001), .in_3(5'b11011),
    .out(multiplexer_4_out));
  Multiplexer #(.Bits(5), .Selector_Bits(2)) multiplexer_5 (
    .sel({X1, X0}), .in_0(multiplexer_1_out), .in_1(multiplexer_2_out), .in_2(multiplexer_3_out),
    .in_3(multiplexer_4_out), .out(Z));
endmodule
