// Digital circuit Exam1_3_Template.dig as structural Verilog
module Exam1_3_Template (
  input  A1,
  input  A2,
  input  A3,
  input  B1,
  input  B2,
  input  B3,
  input  B4,
  output Y
);

  wire and_1_out, and_2_out, and_3_out, and_4_out, and_5_out, and_6_out, and_7_out, and_8_out, and_9_out,
       and_10_out, not_1_out, not_2_out, not_3_out, or_1_out, or_2_out;

  not not_1 (not_1_out, A3);
  not not_2 (not_2_out, A2);
  not not_3 (not_3_out, A1);
  and and_1 (and_1_out, not_1_out, A2, A1);
  and and_2 (and_2_out, A3, A2, not_3_out);
  and and_3 (and_3_out, A3, not_2_out, A1);
  and and_4 (and_4_out, A1, A2, A3);
  and and_5 (and_5_out, B4, B1, ~B2);  // And
  and and_6 (and_6_out, B4, B2);
  and and_7 (and_7_out, ~B4, B3, B2);  // And
  and and_8 (and_8_out, ~B4, ~B3, B2, B1);  // And
  and and_9 (and_9_out, ~B4, B3, ~B2, B1);  // And
  and and_10 (and_10_out, B4, B3, ~B2, ~B1);  // And
  or or_1 (or_1_out, and_1_out, and_2_out, and_3_out, and_4_out);
  or or_2 (or_2_out, and_5_out, and_6_out, and_7_out, and_8_out, and_9_out, and_10_out);
  or or_3 (Y, or_1_out, or_2_out);
endmodule
