// Digital circuit 23_cedt_quiz_1.dig as structural Verilog
module _23_cedt_quiz_1 (
  input  [3:0] in,
  output out
);

  wire and_1_out, and_2_out, and_3_out, and_4_out, not_1_out, not_2_out, not_3_out, not_4_out;

  not not_1 (not_1_out, in[3]);
  not not_2 (not_2_out, in[2]);
  not not_3 (not_3_out, in[1]);
  not not_4 (not_4_out, in[0]);
  and and_1 (and_1_out, not_1_out, in[2], not_3_out, not_4_out);
  and and_2 (and_2_out, not_1_out, not_2_out, in[1], in[0]);
  and and_3 (and_3_out, not_3_out, in[0]);
  and and_4 (and_4_out, in[3], in[1], not_4_out);
  or or_1 (out, and_1_out, and_2_out, and_3_out, and_4_out);
endmodule
