// Digital circuit 23_cedt_quiz_2_2.dig as structural Verilog
module _23_cedt_quiz_2_2 (
  input  [2:0] in0,
  input  [2:0] in1,
  input  addsubtract,
  output [2:0] out
);

  wire [1:0] in0_2bits, in1_2bits;
  wire [2:0] multiplexer_3_out, multiplexer_4_out, multiplexer_5_out, multiplexer_6_out, multiplexer_7_out,
       multiplexer_8_out, multiplexer_9_out, multiplexer_10_out, multiplexer_11_out, multiplexer_12_out;

  Multiplexer #(.Selector_Bits(3), .Bits(2)) multiplexer_1 (
    .sel(in0), .in_0(2'b00), .in_1(2'b01), .in_2(2'b01), .in_3(2'b10), .in_4(2'b01), .in_5(2'b10),
    .in_6(2'b10), .in_7(2'b11), .out(in0_2bits));
  Multiplexer #(.Selector_Bits(3), .Bits(2)) multiplexer_2 (
    .sel(in1), .in_0(2'b00), .in_1(2'b01), .in_2(2'b01), .in_3(2'b10), .in_4(2'b01), .in_5(2'b10),
    .in_6(2'b10), .in_7(2'b11), .out(in1_2bits));
  Multiplexer #(.Selector_Bits(2), .Bits(3)) multiplexer_3 (
    .sel(in1_2bits), .in_0(3'b000), .in_1(3'b001), .in_2(3'b010), .in_3(3'b011), .out(multiplexer_3_out));
  Multiplexer #(.Selector_Bits(2), .Bits(3)) multiplexer_4 (
    .sel(in1_2bits), .in_0(3'b011), .in_1(3'b100), .in_2(3'b101), .in_3(3'b110), .out(multiplexer_4_out));
  Multiplexer #(.Selector_Bits(2), .Bits(3)) multiplexer_5 (
    .sel(in1_2bits), .in_0(3'b000), .in_1(3'b111), .in_2(3'b111), .in_3(3'b111), .out(multiplexer_5_out));
  Multiplexer #(.Selector_Bits(2), .Bits(3)) multiplexer_6 (
    .sel(in1_2bits), .in_0(3'b011), .in_1(3'b010), .in_2(3'b001), .in_3(3'b000), .out(multiplexer_6_out));
  Multiplexer #(.Selector_Bits(2), .Bits(3)) multiplexer_7 (
    .sel(in1_2bits), .in_0(3'b001), .in_1(3'b010), .in_2(3'b011), .in_3(3'b100), .out(multiplexer_7_out));
  Multiplexer #(.Selector_Bits(2), .Bits(3)) multiplexer_8 (
    .sel(in1_2bits), .in_0(3'b010), .in_1(3'b011), .in_2(3'b100), .in_3(3'b101), .out(multiplexer_8_out));
  Multiplexer #(.Selector_Bits(2), .Bits(3)) multiplexer_9 (
    .sel(in1_2bits), .in_0(3'b001), .in_1(3'b000), .in_2(3'b111), .in_3(3'b111), .out(multiplexer_9_out));
  Multiplexer #(.Selector_Bits(2), .Bits(3)) multiplexer_10 (
    .sel(in1_2bits), .in_0(3'b010), .in_1(3'b001), .in_2(3'b000), .in_3(3'b111), .out(multiplexer_10_out));
  Multiplexer #(.Selector_Bits(2), .Bits(3)) multiplexer_11 (
    .sel(in0_2bits), .in_0(multiplexer_3_out), .in_1(multiplexer_7_out), .in_2(multiplexer_8_out),
    .in_3(multiplexer_4_out), .out(multiplexer_11_out));
  Multiplexer #(.Selector_Bits(2), .Bits(3)) multiplexer_12 (
    .sel(in0_2bits), .in_0(multiplexer_5_out), .in_1(multiplexer_9_out), .in_2(multiplexer_10_out),
    .in_3(multiplexer_6_out), .out(multiplexer_12_out));
  Multiplexer #(.Bits(3)) multiplexer_13 (
    .sel(addsubtract), .in_0(multiplexer_11_out), .in_1(multiplexer_12_out), .out(out));

  // Other names for the same wires on the sheet: add = addsubtract
endmodule
