// Digital circuit Q1_exam1_2.dig as structural Verilog
module Q1_exam1_2 (
  input  I0,
  input  I1,
  input  I2,
  output O0,
  output O1,
  output O2
);

  wire and_1_out, and_2_out, and_3_out, and_4_out, and_5_out, and_6_out, not_1_out, not_2_out, not_3_out;

  not not_1 (not_1_out, I0);
  not not_2 (not_2_out, I1);
  not not_3 (not_3_out, I2);
  and and_1 (and_1_out, not_1_out, I1);
  and and_2 (and_2_out, I0, not_2_out);
  and and_3 (and_3_out, not_1_out, not_2_out, I2);
  and and_4 (and_4_out, not_1_out, I1, not_3_out);
  and and_5 (and_5_out, I0, not_2_out, I2);
  and and_6 (and_6_out, I0, I1, not_3_out);
  or or_1 (O1, and_1_out, and_2_out);
  // Or or_2 has open pins: In_1=and_3_out, In_2=and_4_out, In_3=and_5_out, In_4=and_6_out, out=open

  assign O0 = I0;
endmodule
