// Digital circuit counting.dig as structural Verilog
module counting (
  input  clk,
  input  reset,
  output A,
  output B,
  output C
);

  wire and_1_out, and_2_out, and_3_out, and_4_out, and_5_out, and_6_out, and_7_out, or_1_out, or_2_out,
       or_3_out;

  and and_1 (and_1_out, ~reset, ~A, B);  // And
  and and_2 (and_2_out, ~reset, A, C);  // And
  and and_3 (and_3_out, ~reset, ~C, A);  // And
  and and_4 (and_4_out, ~reset, ~A, B, C);  // And
  and and_5 (and_5_out, ~reset, ~A, B, ~C);  // And
  and and_6 (and_6_out, ~reset, C, B);  // And
  and and_7 (and_7_out, ~reset, ~C, ~B);  // And
  or or_1 (or_1_out, and_1_out, and_2_out);
  or or_2 (or_2_out, and_3_out, and_4_out, and_5_out);
  or or_3 (or_3_out, and_6_out, and_7_out);
  D_FF d_ff_1 (.D(or_1_out), .C(clk), .Q(C));  // open: nQ
  D_FF d_ff_2 (.D(or_2_out), .C(clk), .Q(B));  // open: nQ
  D_FF d_ff_3 (.D(or_3_out), .C(clk), .Q(A));  // open: nQ
endmodule
