// Digital circuit cp_01.dig as structural Verilog
module cp_01 (
  input  [7:0] in,
  output out_2,
  output out_3,
  output [2:0] out_4,
  output [2:0] out_5,
  output [2:0] out_6
);

  wire and_1_out, and_3_out, and_4_out, or_1_out, or_2_out, or_3_out;
  wire [2:0] priorityencoder_2_num;

  PriorityEncoder #(.Selector_Bits(3)) priorityencoder_1 (
    .in0(in[0]), .in1(in[1]), .in2(in[2]), .in3(in[3]), .in4(in[4]), .in5(in[5]), .in6(in[6]), .in7(in[7]),
    .num(out_6), .any(out_2));
  PriorityEncoder #(.Selector_Bits(3)) priorityencoder_2 (
    .in0(in[7]), .in1(in[6]), .in2(in[5]), .in3(in[4]), .in4(in[3]), .in5(in[2]), .in6(in[1]), .in7(in[0]),
    .num(priorityencoder_2_num), .any(out_3));
  Multiplexer #(.Selector_Bits(3), .Bits(3)) multiplexer_1 (
    .sel(priorityencoder_2_num), .in_0(3'b111), .in_1(3'b110), .in_2(3'b101), .in_3(3'b100), .in_4(3'b011),
    .in_5(3'b010), .in_6(3'b001), .in_7(3'b000), .out(out_4));
  or or_1 (or_1_out, out_4[0], out_6[0]);
  and and_1 (and_1_out, out_4[0], out_6[0]);
  and and_2 (out_5[0], or_1_out, ~and_1_out);  // And
  or or_2 (or_2_out, out_4[1], out_6[1]);
  and and_3 (and_3_out, out_4[1], out_6[1]);
  or or_3 (or_3_out, out_4[2], out_6[2]);
  and and_4 (and_4_out, or_2_out, ~and_3_out);  // And
  or or_4 (out_5[2], and_3_out, or_3_out);
  or or_5 (out_5[1], and_1_out, and_4_out);

  // Other names for the same wires on the sheet: low[2:0] = out_4; up[2:0] = out_6
endmodule
