// Digital circuit cp_01_2.dig as structural Verilog
module cp_01_2 (
  input  [7:0] in,
  output out_2,
  output out_3,
  output [2:0] out_4,
  output [2:0] out_5
);

  wire [2:0] priorityencoder_2_num;

  PriorityEncoder #(.Selector_Bits(3)) priorityencoder_1 (
    .in0(in[0]), .in1(in[1]), .in2(in[2]), .in3(in[3]), .in4(in[4]), .in5(in[5]), .in6(in[6]), .in7(in[7]),
    .num(out_5), .any(out_2));
  PriorityEncoder #(.Selector_Bits(3)) priorityencoder_2 (
    .in0(in[7]), .in1(in[6]), .in2(in[5]), .in3(in[4]), .in4(in[3]), .in5(in[2]), .in6(in[1]), .in7(in[0]),
    .num(priorityencoder_2_num), .any(out_3));
  Multiplexer #(.Selector_Bits(3), .Bits(3)) multiplexer_1 (
    .sel(priorityencoder_2_num), .in_0(3'b111), .in_1(3'b110), .in_2(3'b101), .in_3(3'b100), .in_4(3'b011),
    .in_5(3'b010), .in_6(3'b001), .in_7(3'b000), .out(out_4));

  // Other names for the same wires on the sheet: low[2:0] = out_4; up[2:0] = out_5
endmodule
